// Logisim project CPU.circ as structural Verilog: 7 circuits, main circuit implementation
module implementation (
  output [7:0] print_R0,
  output [7:0] print_R1,
  output halt
);

  wire ALU0, ALU1, BusControl, clk, comparator_1_eq, comparator_2_eq, IRin, IRout, MARin, MDRin, MDRout,
       MemRead, MemWrite, Offset, or_1_out, out_1, PCin, PCout, R0in, R0out, R1in, R1out, Xin, Zin, Zout;
  wire [2:0] controlled_buffer_3_out;
  wire [7:0] alu_1_alu_out, controlled_buffer_1_out, controlled_buffer_4_out, controlled_buffer_5_out,
       controlled_buffer_6_out, controlled_buffer_8_out, controlled_buffer_10_out, controlled_buffer_12_out,
       controlled_buffer_15_out, controlled_buffer_16_out, IR, MAR_q, MDR_q, memory_dout, multiplexer_1_out,
       PC, register_5_q, signextender_1_se_out, X_q, Z_q;
  wire [7:3] controlled_buffer_3_out_2;

  Clock clock_1 (.out(clk));
  Comparator comparator_1 (.a(PC), .b(8'hf), .eq(comparator_1_eq));  // open: gt, lt
  Comparator comparator_2 (.a(IR), .b({8{1'b0}}), .eq(comparator_2_eq));  // open: gt, lt
  or or_1 (or_1_out, MDRin, MemRead);
  and and_1 (halt, comparator_1_eq, comparator_2_eq);
  assign controlled_buffer_1_out = MDRin ? {controlled_buffer_3_out_2, controlled_buffer_3_out} : 8'bz;  // Controlled_Buffer controlled_buffer_1
  assign controlled_buffer_1_out = MemRead ? memory_dout : 8'bz;  // Controlled_Buffer controlled_buffer_2
  Register #(.trigger("high")) MDR (.D(controlled_buffer_1_out), .en(or_1_out), .clk(clk), .Q(MDR_q));  // open: clr
  assign {controlled_buffer_3_out_2, controlled_buffer_3_out} = MDRout ? MDR_q : 8'bz;  // Controlled_Buffer controlled_buffer_3
  assign controlled_buffer_4_out = MemWrite ? MDR_q : 8'bz;  // Controlled_Buffer controlled_buffer_4
  Register MAR (.D(controlled_buffer_5_out), .en(MARin), .clk(clk), .Q(MAR_q));  // open: clr
  assign controlled_buffer_5_out = MARin ? {controlled_buffer_3_out_2, controlled_buffer_3_out} : 8'bz;  // Controlled_Buffer controlled_buffer_5
  Register register_1 (.D(controlled_buffer_6_out), .en(PCin), .clk(clk), .Q(PC));  // open: clr
  assign controlled_buffer_6_out = PCin ? {controlled_buffer_3_out_2, controlled_buffer_3_out} : 8'bz;  // Controlled_Buffer controlled_buffer_6
  RAM memory (.addr(MAR_q), .we(MemWrite), .oe(MemRead), .clk(clk), .din(controlled_buffer_4_out), .dout(memory_dout));
  assign {controlled_buffer_3_out_2, controlled_buffer_3_out} = PCout ? PC : 8'bz;  // Controlled_Buffer controlled_buffer_7
  assign controlled_buffer_8_out = IRin ? {controlled_buffer_3_out_2, controlled_buffer_3_out} : 8'bz;  // Controlled_Buffer controlled_buffer_8
  Register #(.trigger("high")) register_2 (.D(controlled_buffer_8_out), .en(IRin), .clk(clk), .Q(IR));  // open: clr
  assign {controlled_buffer_3_out_2, controlled_buffer_3_out} = IRout ? IR : 8'bz;  // Controlled_Buffer controlled_buffer_9
  ControlUnit controlunit_1 (
    .clk(clk), .opcode(IR[7:4]), .I3(IR[3]), .I2(IR[2]), .out_5(PCin), .out_6(PCout), .out_7(IRin),
    .out_8(IRout), .R0in(R0in), .R0out(R0out), .out_11(out_1), .R1in(R1in), .R1out(R1out), .out_14(MDRin),
    .out_15(MDRout), .out_16(Zin), .out_17(Zout), .out_18(MARin), .out_19(Xin), .out_20(ALU0), .out_21(ALU1),
    .out_22(MemRead), .out_23(MemWrite), .out_24(BusControl), .out_25(Offset));
  assign controlled_buffer_10_out = R0in ? {controlled_buffer_3_out_2, controlled_buffer_3_out} : 8'bz;  // Controlled_Buffer controlled_buffer_10
  Register register_3 (.D(controlled_buffer_10_out), .en(R0in), .clk(clk), .Q(print_R0));  // open: clr
  assign {controlled_buffer_3_out_2, controlled_buffer_3_out} = R0out ? print_R0 : 8'bz;  // Controlled_Buffer controlled_buffer_11
  Register register_4 (.D(controlled_buffer_12_out), .en(R1in), .clk(clk), .Q(print_R1));  // open: clr
  assign controlled_buffer_12_out = R1in ? {controlled_buffer_3_out_2, controlled_buffer_3_out} : 8'bz;  // Controlled_Buffer controlled_buffer_12
  assign {controlled_buffer_3_out_2, controlled_buffer_3_out} = R1out ? print_R1 : 8'bz;  // Controlled_Buffer controlled_buffer_13
  Register register_5 (.D(8'h1), .en(1'b1), .clk(clk), .Q(register_5_q));  // open: clr
  assign {controlled_buffer_3_out_2, controlled_buffer_3_out} = out_1 ? register_5_q : 8'bz;  // Controlled_Buffer controlled_buffer_14
  SignExtender signextender_1 (
    .ir02(controlled_buffer_3_out), .ir3(controlled_buffer_3_out_2[3]), .offset(Offset),
    .se_out(signextender_1_se_out));
  Multiplexer #(.enable("false"), .width(8)) multiplexer_1 (
    .in0(signextender_1_se_out), .in1({controlled_buffer_3_out_2, controlled_buffer_3_out}),
    .out(multiplexer_1_out), .sel(BusControl));
  Register Z (.D(controlled_buffer_15_out), .en(Zin), .clk(clk), .Q(Z_q));  // open: clr
  assign controlled_buffer_15_out = Zin ? alu_1_alu_out : 8'bz;  // Controlled_Buffer controlled_buffer_15
  assign controlled_buffer_16_out = Xin ? {controlled_buffer_3_out_2, controlled_buffer_3_out} : 8'bz;  // Controlled_Buffer controlled_buffer_16
  assign {controlled_buffer_3_out_2, controlled_buffer_3_out} = Zout ? Z_q : 8'bz;  // Controlled_Buffer controlled_buffer_17
  Register X (.D(controlled_buffer_16_out), .en(Xin), .clk(clk), .Q(X_q));  // open: clr
  ALU alu_1 (.A(X_q), .B(multiplexer_1_out), .ALU0(ALU0), .ALU1(ALU1), .ALU_OUT(alu_1_alu_out));

  // Other names for the same wires on the sheet: OPCODE[3:0] = IR[7:4]; R0[7:0] = print_R0; R1[7:0] = print_R1
endmodule

module ALU (
  input  [7:0] A,
  input  [7:0] B,
  input  ALU0,
  input  ALU1,
  output [7:0] ALU_OUT
);

  wire [7:0] adder_1_out, multiplier_1_out, nand_1_out, subtractor_1_out;

  Adder adder_1 (.a(A), .b(B), .out(adder_1_out));  // open: cin, cout
  Subtractor subtractor_1 (.a(A), .b(B), .out(subtractor_1_out));  // open: bin, bout
  Multiplier multiplier_1 (.a(A), .b(B), .out(multiplier_1_out));  // open: cin, cout
  assign nand_1_out = ~(A & B);  // NAND_Gate nand_1, 8 bits wide
  Multiplexer #(.enable("false"), .select(2), .width(8)) multiplexer_1 (
    .in0(nand_1_out), .in1(subtractor_1_out), .in2(multiplier_1_out), .in3(adder_1_out), .out(ALU_OUT),
    .sel({ALU1, ALU0}));
endmodule

module SignExtender (
  input  [2:0] ir02,
  input  ir3,
  input  offset,
  output [7:0] se_out
);

  and and_1 (se_out[7], ir3, offset);

  assign se_out[6:0] = {{4{se_out[7]}}, ir02};
endmodule

module ControlUnit (
  input  clk,
  input  [3:0] opcode,
  input  I3,
  input  I2,
  output out_5,
  output out_6,
  output out_7,
  output out_8,
  output R0in,
  output R0out,
  output out_11,
  output R1in,
  output R1out,
  output out_14,
  output out_15,
  output out_16,
  output out_17,
  output out_18,
  output out_19,
  output out_20,
  output out_21,
  output out_22,
  output out_23,
  output out_24,
  output out_25
);

  wire signallogic_1_rdsin, signallogic_1_rdsout, signallogic_1_rsin, signallogic_1_rsout;
  wire [4:0] NextState, StateRegister_q;

  Register #(.width(5)) StateRegister (.D(NextState), .en(1'b1), .clk(clk), .Q(StateRegister_q));  // open: clr
  NextStateLogic nextstatelogic_1 (.currentstate(StateRegister_q), .opcode(opcode), .nextstate(NextState));
  SignalLogic signallogic_1 (
    .state(StateRegister_q), .opcode(opcode), .PCin(out_5), .PCout(out_6), .IRin(out_7), .IRout(out_8),
    .Rdsin(signallogic_1_rdsin), .Rdsout(signallogic_1_rdsout), .OUT_1(out_11), .Rsin(signallogic_1_rsin),
    .Rsout(signallogic_1_rsout), .MDRin(out_14), .MDRout(out_15), .Zin(out_16), .Zout(out_17),
    .MARin(out_18), .Xin(out_19), .ALU0(out_20), .ALU1(out_21), .MemRead(out_22), .MemWrite(out_23),
    .BusControl(out_24), .Offset(out_25));
  RegSelect regselect_1 (
    .Rsin(signallogic_1_rsin), .Rdsin(signallogic_1_rdsin), .Rsout(signallogic_1_rsout),
    .Rdsout(signallogic_1_rdsout), .i3(I3), .i2(I2), .R0in(R0in), .R0out(R0out), .R1in(R1in), .R1out(R1out));

  // Other names for the same wires on the sheet: ALU0 = out_20; ALU1 = out_21; BusControl = out_24; IRin = out_7;
  //   IRout = out_8; MARin = out_18; MDRin = out_14; MDRout = out_15; MemRead = out_22; MemWrite = out_23;
  //   Offset = out_25; out_1 = out_11; PCin = out_5; PCout = out_6; Xin = out_19; Zin = out_16; Zout = out_17
endmodule

module RegSelect (
  input  Rsin,
  input  Rdsin,
  input  Rsout,
  input  Rdsout,
  input  i3,
  input  i2,
  output R0in,
  output R0out,
  output R1in,
  output R1out
);

  wire and_1_out, and_2_out, and_3_out, and_4_out, and_5_out, and_6_out, and_7_out, and_8_out, not_1_out,
       not_2_out;

  not not_1 (not_1_out, i3);
  not not_2 (not_2_out, i2);
  and and_1 (and_1_out, not_1_out, Rdsin);
  or or_1 (R0in, and_1_out, and_2_out);
  and and_2 (and_2_out, not_2_out, Rsin);
  and and_3 (and_3_out, not_1_out, Rdsout);
  or or_2 (R0out, and_3_out, and_4_out);
  and and_4 (and_4_out, not_2_out, Rsout);
  and and_5 (and_5_out, i3, Rdsin);
  and and_6 (and_6_out, i2, Rsin);
  or or_3 (R1in, and_5_out, and_6_out);
  and and_7 (and_7_out, i3, Rdsout);
  and and_8 (and_8_out, i2, Rsout);
  or or_4 (R1out, and_7_out, and_8_out);
endmodule

module SignalLogic (
  input  [4:0] state,
  input  [3:0] opcode,
  output PCin,
  output PCout,
  output IRin,
  output IRout,
  output Rdsin,
  output Rdsout,
  output OUT_1,
  output Rsin,
  output Rsout,
  output MDRin,
  output MDRout,
  output Zin,
  output Zout,
  output MARin,
  output Xin,
  output ALU0,
  output ALU1,
  output MemRead,
  output MemWrite,
  output BusControl,
  output Offset
);

  wire and_1_out, and_2_out, ISADD, ISADDI, ISADDM, ISJMP, ISNAND, ISSUB, or_1_out, S0, S2, S4, S5, S6, S7,
       S8, S9, S10, S12, S13, S14, S15, S16;

  Decoder #(.select(5)) decoder_1 (
    .out0(S0), .out1(OUT_1), .out2(S2), .out3(IRin), .out4(S4), .out5(S5), .out6(S6), .out7(S7), .out8(S8),
    .out9(S9), .out10(S10), .out11(Offset), .out12(S12), .out13(S13), .out14(S14), .out15(S15), .out16(S16),
    .out17(MDRin), .sel(state), .en(1'b1));  // open: out18, out19, out20, out21, out22, out23, out24, out25, out26, out27, out28, out29, out30, out31
  Decoder #(.select(4)) decoder_2 (
    .out0(ISNAND), .out1(ISADD), .out2(ISADDM), .out3(ISADDI), .out4(ISSUB), .out15(ISJMP), .sel(opcode),
    .en(1'b1));  // open: out5, out6, out7, out8, out9, out10, out11, out12, out13, out14
  or or_1 (or_1_out, ISADD, ISSUB);
  and and_1 (and_1_out, or_1_out, S5);
  or or_2 (Zout, S2, S6, S9, S12, S16);
  or or_3 (ALU0, OUT_1, S8, Offset, S15, and_1_out);
  and and_2 (and_2_out, ISADD, S5);
  or or_4 (Rdsout, S4, S7, S14);
  or or_5 (Rdsin, S6, S9, S16);
  or or_6 (Zin, OUT_1, S5, S8, Offset, S15);
  or or_7 (ALU1, OUT_1, S8, Offset, S15, and_2_out);
  or or_8 (PCin, S2, S12);
  or or_9 (Xin, S0, S4, S7, S10, S14);
  or or_10 (PCout, S0, S10);
  or or_11 (IRout, S8, Offset);
  or or_12 (Rsout, S5, S13);
  or or_13 (MDRout, IRin, S15);
  or or_14 (MARin, S0, S13);
  or or_15 (MemRead, S0, OUT_1, S2, S13, S14);
  or or_16 (BusControl, OUT_1, S5, S15);

  assign MemWrite = 1'b0;
  assign Rsin = 1'b0;

  // Other names for the same wires on the sheet: S1 = OUT_1; S3 = IRin; S11 = Offset; S17 = MDRin
endmodule

module NextStateLogic (
  input  [4:0] currentstate,
  input  [3:0] opcode,
  output [4:0] nextstate
);

  wire and_1_out, and_2_out, and_3_out, and_4_out, ISADD, ISADDI, ISADDM, ISJMP, ISNAND, ISSUB, or_1_out,
       or_2_out, S0, S1, S2, S3, S4, S5, S6, S7, S8, S9, S10, S11, S12, S13, S14, S15, S16;

  Decoder #(.select(5)) decoder_1 (
    .out0(S0), .out1(S1), .out2(S2), .out3(S3), .out4(S4), .out5(S5), .out6(S6), .out7(S7), .out8(S8),
    .out9(S9), .out10(S10), .out11(S11), .out12(S12), .out13(S13), .out14(S14), .out15(S15), .out16(S16),
    .sel(currentstate), .en(1'b1));  // open: out17, out18, out19, out20, out21, out22, out23, out24, out25, out26, out27, out28, out29, out30, out31
  Decoder #(.select(4)) decoder_2 (
    .out0(ISNAND), .out1(ISADD), .out2(ISADDM), .out3(ISADDI), .out4(ISSUB), .out15(ISJMP), .sel(opcode),
    .en(1'b1));  // open: out5, out6, out7, out8, out9, out10, out11, out12, out13, out14
  and and_1 (and_1_out, S3, ISJMP);
  and and_2 (and_2_out, S3, ISADDM);
  or or_1 (or_1_out, ISADD, ISSUB, ISNAND);
  and and_3 (and_3_out, S3, or_1_out);
  and and_4 (and_4_out, S3, ISADDI);
  or or_2 (or_2_out, S6, S9, S12, S16);
  Priority_Encoder #(.select(5)) priority_encoder_1 (
    .in0(or_2_out), .in1(S0), .in2(S1), .in3(S2), .in4(and_3_out), .in5(S4), .in6(S5), .in7(and_4_out),
    .in8(S7), .in9(S8), .in10(and_1_out), .in11(S10), .in12(S11), .in13(and_2_out), .in14(S13), .in15(S14),
    .in16(S15), .out(nextstate));  // open: in17, in18, in19, in20, in21, in22, in23, in24, in25, in26, in27, in28, in29, in30, in31, gs, en_out, en_in
endmodule
